# Fritzing sketch MyFlightControll (saved by Fritzing 0.9.3b)

parts:
  Bauteil2 = Arduino Nano (Rev3.0)
  GY2 = MPU-6050 Board GY-521 [form="♀ (female)" package=THT]
  J3 = FS-IA6 [form="♂ (shrouded male)" package=THT]  # not connected
  M3 = ESC
  920KV_Motor3 = DJI 920 KV Motor
  BATT2 = LiPoly Battery (1300mAh)
  LED2 = smd LED [color="Red (633nm)" package="0603 [SMD]"]
  R2 = Resistor [tolerance=±5% resistance=330 package=THT]
  M4 = ESC
  920KV_Motor4 = DJI 920 KV Motor
  M5 = ESC
  M6 = ESC
  920KV_Motor5 = DJI 920 KV Motor
  920KV_Motor6 = DJI 920 KV Motor
  Part2 = Bluetooth HC-05 Macho

nets:
  N1: Bauteil2.D1/TX, Part2.RXD
  N2: Bauteil2.D0/RX, Part2.TXD
  N3: Bauteil2.D3, M6.DATA
  N4: Bauteil2.D8, R2.Pin_1
  N5: Bauteil2.D9, M5.DATA
  N6: Bauteil2.D10, M4.DATA
  N7: Bauteil2.D11/MOSI, M3.DATA
  N8: Bauteil2.VIN, BATT2.positive
  N9: Bauteil2.GND, GY2.pin2
  N10: Bauteil2.5V, GY2.pin1
  N11: Bauteil2.A5, GY2.pin3
  N12: Bauteil2.A4, GY2.pin4
  N13: M3.U, 920KV_Motor3.u
  N14: M3.V, 920KV_Motor3.v
  N15: M3.W, 920KV_Motor3.w
  N16: LED2.anode, R2.Pin_0
  N17: M4.U, 920KV_Motor4.u
  N18: M4.V, 920KV_Motor4.v
  N19: M4.W, 920KV_Motor4.w
  N20: M5.U, 920KV_Motor5.u
  N21: M5.V, 920KV_Motor5.v
  N22: M5.W, 920KV_Motor5.w
  GND: M5.GND, M6.GND
  N23: M6.U, 920KV_Motor6.u
  N24: M6.V, 920KV_Motor6.v
  N25: M6.W, 920KV_Motor6.w

custom parts:
  MPU-6050 Board GY-521: Acelerometro y Giroscopio MPU-6050 Board GY-521
  FS-IA6: FlySky FS-IA6 Receiver
  DJI 920 KV Motor: DJI Brushless Outrunner 2212/920K Motor F330-550
  LiPoly Battery (1300mAh): Lithium Ion Polymer Battery (1300mAh)
